// Logisim project Ammar --Final.circ as structural Verilog: 7 circuits, main circuit main
module main (
  input  Enable,
  input  Reset,
  output c1,
  output c0,
  output not_found,
  output found
);

  wire and_1_out, and_2_out, Clock_out, expected_output_1_out_5, not_2_out, not_4_out, not_5_out, or_1_out,
       test_ic_1_all_valid, test_ic_1_output, validate_1_out_3;
  wire [1:0] Main_Counter_q;
  wire [3:2] not_1_out;

  Clock Clock (.out(Clock_out));
  and and_1 (and_1_out, or_1_out, not_2_out);
  and and_2 (and_2_out, validate_1_out_3, Enable, or_1_out, not_found);
  Counter #(.width(4), .max('hf), .ongoal("continue")) Main_Counter (
    .load(and_1_out), .D({not_1_out, 2'b00}), .count(and_2_out), .Q({c1, c0, Main_Counter_q}),
    .clk(Clock_out), .clr(Reset));  // open: carry
  not not_1 (not_1_out[2], c0);
  expected_output expected_output_1 (
    .Test_Case_0(Main_Counter_q[1]), .Test_Case_1(Main_Counter_q[0]), .IC_Type_1(c1), .IC_Type_0(c0),
    .out_5(expected_output_1_out_5));
  xor xor_1 (not_1_out[3], c0, c1);
  not not_2 (not_2_out, validate_1_out_3);
  and and_3 (found, validate_1_out_3, Main_Counter_q[1], Main_Counter_q[0]);
  Test_Ic test_ic_1 (
    .A(Main_Counter_q[1]), .B(Main_Counter_q[0]), .Output(test_ic_1_output), .all_valid(test_ic_1_all_valid));
  or or_1 (or_1_out, validate_1_out_3, not_5_out, not_4_out);
  not not_3 (not_found, found);
  not not_4 (not_4_out, c0);
  not not_5 (not_5_out, c1);
  Validate validate_1 (.in_1(test_ic_1_output), .in_2(expected_output_1_out_5), .out_3(validate_1_out_3));

  // Notes on the sheet:
  //   all valid
endmodule

// Expected Output
module expected_output (
  input  Test_Case_0,
  input  Test_Case_1,
  input  IC_Type_1,
  input  IC_Type_0,
  output out_5
);

  wire and_1_out, nand_1_out, or_1_out, xor_1_out;

  or or_1 (or_1_out, Test_Case_0, Test_Case_1);
  xor xor_1 (xor_1_out, Test_Case_0, Test_Case_1);
  nand nand_1 (nand_1_out, Test_Case_0, Test_Case_1);
  and and_1 (and_1_out, Test_Case_0, Test_Case_1);
  Multiplexer #(.select(2)) multiplexer_1 (
    .in0(and_1_out), .in1(or_1_out), .in2(xor_1_out), .in3(nand_1_out), .out(out_5),
    .sel({IC_Type_1, IC_Type_0}));  // open: en
endmodule

module Validate (
  input  in_1,
  input  in_2,
  output out_3
);

  xnor xnor_1 (out_3, in_1, in_2);
endmodule

module Success (
  input  Enable,
  input  validate,
  input  reset,
  output Q
);

  wire and_1_out;

  and and_1 (and_1_out, Q, validate);
  D_Flip_Flop d_ff_1 (.clk(Enable), .D(and_1_out), .Q(Q), .preset(reset), .en(Enable));  // open: Qn, reset

  // Notes on the sheet:
  //   this AND is only for simulation
endmodule

module _2_4_MUX (
  input  C0,
  input  C1,
  input  I0,
  input  I1,
  input  I2,
  input  I3,
  output O
);

  wire and_1_out, and_2_out, and_3_out, and_4_out, not_1_out, not_2_out, not_3_out, not_4_out;

  not not_1 (not_1_out, C0);
  not not_2 (not_2_out, C1);
  not not_3 (not_3_out, C0);
  not not_4 (not_4_out, C1);
  and and_1 (and_1_out, not_1_out, not_2_out, I0);
  and and_2 (and_2_out, not_3_out, C1, I1);
  and and_3 (and_3_out, C0, not_4_out, I2);
  and and_4 (and_4_out, C0, C1, I3);
  or or_1 (O, and_1_out, and_2_out, and_3_out, and_4_out);
endmodule

// Test IC
module Test_Ic (
  input  A,
  input  B,
  output Output,
  output all_valid
);

  wire and_2_out, and_3_out, and_4_out, xnor_1_out, xnor_2_out;

  and and_1 (Output, A, B);
  and and_2 (and_2_out, A, B);
  and and_3 (and_3_out, A, B);
  and and_4 (and_4_out, A, B);
  xnor xnor_1 (xnor_1_out, Output, and_2_out);
  xnor xnor_2 (xnor_2_out, and_3_out, and_4_out);
  and and_5 (all_valid, xnor_1_out, xnor_2_out);
  // NAND_Gate nand_1 is placed but not wired
  // NAND_Gate nand_2 is placed but not wired
  // NAND_Gate nand_3 is placed but not wired
  // NAND_Gate nand_4 is placed but not wired
  // XOR_Gate xor_1 is placed but not wired
  // XOR_Gate xor_2 is placed but not wired
  // XOR_Gate xor_3 is placed but not wired
  // XOR_Gate xor_4 is placed but not wired
  // OR_Gate or_1 is placed but not wired
  // OR_Gate or_2 is placed but not wired
  // OR_Gate or_3 is placed but not wired
  // OR_Gate or_4 is placed but not wired
  // AND_Gate and_6 is placed but not wired
  // AND_Gate and_7 is placed but not wired
  // AND_Gate and_8 is placed but not wired
  // AND_Gate and_9 is placed but not wired

  // Notes on the sheet:
  //   11
  //   10
  //   01
  //   00
endmodule

module optimiseCounter (
  input  f,
  input  v,
  input  c1,
  input  c2,
  input  c3,
  input  c4,
  output l,
  output e
);

  wire not_1_out, not_2_out, not_3_out, not_4_out, or_1_out;

  not not_1 (not_1_out, c1);
  not not_2 (not_2_out, c2);
  not not_3 (not_3_out, f);
  or or_1 (or_1_out, not_1_out, not_2_out);
  not not_4 (not_4_out, v);
  and and_1 (e, not_3_out, v);
  and and_2 (l, or_1_out, not_4_out);
endmodule
