// Logisim project main.circ as structural Verilog: 4 circuits, main circuit main
module main (
  input  Enable,
  input  Reset,
  output c0,
  output c1,
  output not_found,
  output found
);

  wire and_1_out, and_2_out, Clock_out, expected_output_1_out_3, nand_1_out, validate_1_out_3;
  wire [1:0] Main_Counter_2_q;

  Clock Clock (.out(Clock_out));
  and and_1 (and_1_out, Clock_out, not_found, Enable);
  nand nand_1 (nand_1_out, Main_Counter_2_q[0], Main_Counter_2_q[1]);
  Counter #(.width(2), .max('h3)) Main_Counter (
    .count(1'b1), .Q({c1, c0}), .clk(nand_1_out), .clr(Reset));  // open: load, D, carry
  Counter #(.width(2), .max('h3), .ongoal("continue")) Main_Counter_2 (
    .count(1'b1), .Q(Main_Counter_2_q), .clk(and_1_out), .clr(Reset));  // open: load, D, carry
  expected_output expected_output_1 (.in_1({c1, c0}), .in_2(Main_Counter_2_q), .out_3(expected_output_1_out_3));
  and and_2 (and_2_out, Main_Counter_2_q[0], Main_Counter_2_q[1]);
  Validate validate_1 (.in_1(and_2_out), .in_2(expected_output_1_out_3), .out_3(validate_1_out_3));
  Success success_1 (.validate(validate_1_out_3), .found(found), .not_found(not_found));  // open: clk
  // AND_Gate and_3 is placed but not wired
  // OR_Gate or_1 is placed but not wired
  // XOR_Gate xor_1 is placed but not wired
  // NAND_Gate nand_2 is placed but not wired

  // Notes on the sheet:
  //   Expected Output
  //   Test IC
  //   success
  //   validate
endmodule

module expected_output (
  input  [1:0] in_1,
  input  [1:0] in_2,
  output out_3
);


  assign out_3 = 1'b1;

  // Notes on the sheet:
  //   this is not complete yet
endmodule

module Validate (
  input  in_1,
  input  in_2,
  output out_3
);


  assign out_3 = 1'b1;

  // Notes on the sheet:
  //   not complete
endmodule

module Success (
  input  clk,
  input  validate,
  output found,
  output not_found
);

  wire and_1_out;

  and and_1 (and_1_out, validate, found);
  D_Flip_Flop d_ff_1 (.clk(clk), .D(and_1_out), .Q(found), .Qn(not_found));  // open: preset, en, reset
endmodule
